// Logisim project 16 bit computer.circ as structural Verilog
module CPU (
  input  in_1,
  output [7:0] out_2,
  output [7:0] out_3
);

  wire clock_1_out, n2_cycle_1_trigger;
  wire [7:0] ram_1_data, transistor_1_out;
  wire [15:0] counter_1_q;

  Counter #(.width(16), .max('hffff), .trigger("falling")) counter_1 (
    .count(in_1), .Q(counter_1_q), .clk(clock_1_out));  // open: load, D, carry, clr
  Clock clock_1 (.out(clock_1_out));
  RAM #(.addrWidth(16)) ram_1 (.addr(counter_1_q), .data(ram_1_data), .clk(clock_1_out));  // open: sel, ld, clr
  Transistor #(.\type ("n"), .width(8)) transistor_1 (
    .in(ram_1_data), .out(transistor_1_out), .gate(n2_cycle_1_trigger));
  _2_cycle u_2_cycle_1 (.Active(ram_1_data[7]), .CLK(clock_1_out), .Trigger(n2_cycle_1_trigger));
  Register register_1 (
    .mov_al_value8(n2_cycle_1_trigger), .Data_In(transistor_1_out), .CLK(clock_1_out), .ah(out_2), .al(out_3));  // open: mov_ah_value8
endmodule

module Register (
  input  mov_ah_value8,
  input  mov_al_value8,
  input  [7:0] Data_In,
  input  CLK,
  output [7:0] ah,
  output [7:0] al
);

  wire [7:0] transistor_1_out, transistor_2_out;

  Transistor #(.\type ("n"), .width(8)) transistor_1 (.in(Data_In), .out(transistor_1_out), .gate(mov_ah_value8));
  Transistor #(.\type ("n"), .width(8)) transistor_2 (.in(Data_In), .out(transistor_2_out), .gate(mov_al_value8));
  Register_part u_ah (.D(transistor_1_out), .en(mov_ah_value8), .Q(ah), .clk(CLK));  // open: clr
  Register_part u_al (.D(transistor_2_out), .en(mov_al_value8), .Q(al), .clk(CLK));  // open: clr
endmodule

module _2_cycle (
  input  Active,
  input  CLK,
  output Trigger
);

  wire and_1_out, d_ff_1_qn, or_1_out, t_ff_1_q;

  D_Flip_Flop d_ff_1 (
    .clk(CLK), .D(and_1_out), .Q(Trigger), .Qn(d_ff_1_qn), .en(or_1_out), .reset(t_ff_1_q));  // open: preset
  and and_1 (and_1_out, ~Trigger, Active);  // AND_Gate
  or or_1 (or_1_out, and_1_out, t_ff_1_q);
  T_Flip_Flop t_ff_1 (.clk(CLK), .T(Trigger), .Q(t_ff_1_q), .reset(d_ff_1_qn), .en(CLK));  // open: Qn, preset
endmodule
